// Logisim project CPU_model.circ as structural Verilog: 1 circuit, main circuit main
module main (
  input  Clear_All,
  input  Clear_RAM,
  output [7:0] out_3
);

  wire and_1_out, and_2_out, buffer_1_out, clock_1_out, controlled_inverter_2_out, not_1_out, not_2_out,
       or_1_out, or_2_out, or_3_out, or_4_out, pull_resistor_1_node, register_2_q, ZFLAG_q;
  wire [2:0] Step_Counter_q;
  wire [3:0] AR_q, bit_extender_1_out, bit_extender_3_out, bit_extender_5_out, bit_extender_6_out,
       bit_extender_7_out, bit_extender_8_out, IP_q;
  wire [7:0] adder_1_out, AH_q, AL_q, bit_extender_2_out, bit_extender_4_out, divider_1_out, divider_1_rem,
       divider_2_out, divider_2_rem, IR_q, pull_resistor_4_node, register_1_q, xnor_1_out, xor_1_out;
  wire [7:7] rom_1_data_2;
  wire [19:0] rom_1_data;

  Pull_Resistor pull_resistor_1 (.node(pull_resistor_1_node));
  or or_1 (or_1_out, rom_1_data[17], and_1_out);
  and and_1 (and_1_out, rom_1_data[10], or_2_out);
  assign pull_resistor_1_node = rom_1_data[14] ? ~ZFLAG_q : 1'bz;  // Controlled_Inverter controlled_inverter_1
  or or_2 (or_2_out, pull_resistor_1_node, controlled_inverter_2_out);
  assign controlled_inverter_2_out = rom_1_data[16] ? ~register_2_q : 1'bz;  // Controlled_Inverter controlled_inverter_2
  Pull_Resistor pull_resistor_2 (.node(controlled_inverter_2_out));
  or or_3 (or_3_out, buffer_1_out, Clear_All);
  buf buffer_1 (buffer_1_out, rom_1_data[18]);
  Bit_Extender #(.out_width(4)) bit_extender_1 (.in(out_3), .out(bit_extender_1_out));
  Register IR (.D(out_3), .en(rom_1_data[4]), .Q(IR_q), .clk(clock_1_out), .clr(Clear_All));
  Counter #(.width(3), .max('h7), .ongoal("load")) Step_Counter (
    .Q(Step_Counter_q), .clk(not_1_out), .clr(or_3_out));  // open: load, D, count, carry
  not not_1 (not_1_out, clock_1_out);
  assign bit_extender_2_out = {{4{1'b0}}, IP_q};  // Bit_Extender bit_extender_2
  Counter #(.width(4), .max('hf)) IP (
    .load(or_1_out), .D(bit_extender_1_out), .count(rom_1_data[9]), .Q(IP_q), .clk(clock_1_out),
    .clr(Clear_All));  // open: carry
  Bit_Extender #(.out_width(4)) bit_extender_3 (.in(IR_q), .out(bit_extender_3_out));
  ROM #(.addrWidth(7), .dataWidth(20)) rom_1 (
    .addr({IR_q[7:4], Step_Counter_q}), .data({rom_1_data[19:13], rom_1_data_2[7], rom_1_data[11:0]}));  // open: sel
  assign out_3 = rom_1_data[8] ? bit_extender_2_out : 8'bz;  // Controlled_Buffer controlled_buffer_1
  assign out_3 = rom_1_data[3] ? bit_extender_4_out : 8'bz;  // Controlled_Buffer controlled_buffer_2
  assign bit_extender_4_out = {{4{1'b0}}, bit_extender_3_out};  // Bit_Extender bit_extender_4
  Register register_1 (.D(out_3), .en(rom_1_data[19]), .Q(register_1_q), .clk(clock_1_out), .clr(Clear_All));
  Divider divider_1 (.a(register_1_q), .b(8'h64), .out(divider_1_out), .rem(divider_1_rem));  // open: upper
  Divider divider_2 (.a(divider_1_rem), .b(8'ha), .out(divider_2_out), .rem(divider_2_rem));  // open: upper
  Hex_Digit_Display hex_digit_display_1 (.value(bit_extender_5_out));  // open: dp
  Bit_Extender #(.out_width(4)) bit_extender_5 (.in(divider_1_out), .out(bit_extender_5_out));
  Clock clock_1 (.out(clock_1_out));
  Hex_Digit_Display hex_digit_display_2 (.value(bit_extender_7_out));  // open: dp
  Hex_Digit_Display hex_digit_display_3 (.value(bit_extender_6_out));  // open: dp
  Bit_Extender #(.out_width(4)) bit_extender_6 (.in(divider_2_out), .out(bit_extender_6_out));
  Bit_Extender #(.out_width(4)) bit_extender_7 (.in(divider_2_rem), .out(bit_extender_7_out));
  Pull_Resistor pull_resistor_3 (.node(out_3));
  assign out_3 = rom_1_data[0] ? adder_1_out : 8'bz;  // Controlled_Buffer controlled_buffer_3
  assign out_3 = rom_1_data[11] ? AH_q : 8'bz;  // Controlled_Buffer controlled_buffer_4
  Register AH (.D(out_3), .en(rom_1_data[2]), .Q(AH_q), .clk(clock_1_out), .clr(Clear_All));
  Register AL (.D(out_3), .en(rom_1_data[1]), .Q(AL_q), .clk(clock_1_out), .clr(Clear_All));
  Bit_Extender #(.out_width(4)) bit_extender_8 (.in(out_3), .out(bit_extender_8_out));
  Adder adder_1 (.a(AH_q), .b(xor_1_out), .out(adder_1_out), .cin(rom_1_data_2[7]));  // open: cout
  assign xor_1_out = AL_q ^ {8{rom_1_data_2[7]}};  // XOR_Gate xor_1, 8 bits wide
  Register #(.width(4)) AR (.D(bit_extender_8_out), .en(rom_1_data[7]), .Q(AR_q), .clk(clock_1_out), .clr(Clear_All));
  Pull_Resistor pull_resistor_4 (.node(pull_resistor_4_node));
  not not_2 (not_2_out, xnor_1_out[7]);
  assign xnor_1_out = ~(adder_1_out ^ pull_resistor_4_node);  // XNOR_Gate xnor_1, 8 bits wide
  or or_4 (or_4_out, rom_1_data[6], rom_1_data[5]);
  RAM #(.addrWidth(4), .bus("separate")) ram_1 (
    .addr(AR_q), .din(out_3), .data(out_3), .str(rom_1_data[5]), .sel(or_4_out), .clk(clock_1_out),
    .ld(rom_1_data[6]), .clr(Clear_RAM));
  Register #(.width(1)) register_2 (
    .D(not_2_out), .en(rom_1_data[15]), .Q(register_2_q), .clk(clock_1_out), .clr(Clear_All));
  Register #(.width(1)) ZFLAG (.D(and_2_out), .en(rom_1_data[13]), .Q(ZFLAG_q), .clk(clock_1_out), .clr(Clear_All));
  and and_2 (and_2_out, xnor_1_out[7], xnor_1_out[6], xnor_1_out[5], xnor_1_out[4], xnor_1_out[3], xnor_1_out[2], xnor_1_out[1], xnor_1_out[0]);

  // Notes on the sheet:
  //   ROM (Decoder)
  //   contents of rom_1 (hex, n*v repeats v):
  //   180 250 88 44 180 0 0 0 180 250 88 42 5 0 0 0 180 250 88 820 4*0 180 250 88 42 b005 0 0 0 180 250 c
  //   5*0 180 250 88 42 b001 0 0 0 180 250 20408 5*0 180 250 4408 5*0 180 250 10408 408 5*0 80800 50 40000
  //   4*0 180 250 6*0 180 250 6*0 180 250 6*0 180 250 6*0 180 250 6*0 180 50
  //   Out IP
  //   Clear IP
  //   Clocking IP
  //   Input IP
  //   Out IR
  //   Input IR
  //   Clear IR
  //   Clocking IR
  //   Clear IP
  //   Clocking IP
  //   Out Sum
  //   Input AL
  //   Input AH
  //   Out IR
  //   Input IR
  //   Write RAM
  //   Read RAM
  //   Input AR
  //   Out IP
  //   Incr/decr IP
  //   Load IP
  //   Out AH
  //   Sign extension
  //   Input ZFLAG
  //   Out ZFLAG
  //   Input NFLAG
  //   Out NFLAG
  //   Direct Input Ip
  //   Clear Step Counter
  //   Input Display
  //   RAM output
  //   Write to RAM
  //   Load AR
  //   Clocking AR
  //   Clear AR
  //   Clocking input RAM
  //   Output Sum
  //   Output AH
  //   Input Data AH
  //   Clocking АH
  //   Clear AH
  //   Input Data AL
  //   Clocking AL
  //   Clear AL
  //   RAM
  //   NFLAG
endmodule
